# Fritzing sketch Wiring (saved by Fritzing 1.0.4)
breadboards: 1

parts:
  Arduino = Arduino Uno (Rev3)
  Sensor_A = HC-SR04 Ultrasonic Distance Sensor
  Sensor_B = HC-SR04 Ultrasonic Distance Sensor
  Buzzer = Piezo Speaker
  VCC1 = 4 x AA Battery Box [internal_resistance=0.1Ω]  # not connected

nets:
  N1: Arduino.D9_PWM, Sensor_A.TRIG
  N2: Arduino.D10_PWM/SS, Sensor_A.ECHO
  N3: Arduino.D11_PWM/MOSI, Sensor_B.TRIG
  N4: Arduino.D12/MISO, Sensor_B.ECHO
  VCC: Arduino.5V, Sensor_A.VCC, Sensor_B.VCC
  GND: Arduino.GND, Sensor_A.GND, Sensor_B.GND, Buzzer.pin1

custom parts:
  4 x AA Battery Box: A 4 x AA battery box.
